// Logisim project Baguetteboard - Gisen.circ as structural Verilog: 9 circuits, main circuit ALU
module Computer_ImTheBeemoPlush (
  input  in_1,
  input  in_2,
  input  in_3,
  input  in_4,
  input  in_5,
  input  in_6,
  input  in_7,
  input  in_8,
  input  in_9,
  input  in_10,
  input  in_11,
  input  in_12,
  input  in_13,
  input  in_14,
  input  in_15,
  input  in_16,
  input  in_17,
  input  in_18,
  input  in_19,
  input  in_20,
  input  in_21,
  input  in_22,
  input  in_23,
  input  in_24,
  input  in_25,
  input  in_26,
  input  in_27,
  input  in_28,
  input  in_29,
  input  in_30,
  input  in_31,
  input  in_32,
  input  in_33
);

  wire button_2_out, CLK, INAwe, INBwe, INSTwe, MADwe, MEMwe, MR, REGwe;
  wire [1:0] dipswitch_1_sw2;
  wire [3:0] FLAGS, STEP;
  wire [4:0] OPCODE;
  wire [7:0] ALU_A, ALU_B, ALU_OUTPUT, bit_extender_1_out, controlled_buffer_1_out, controlled_buffer_5_out,
       controlled_buffer_6_out, inst_decoder_1_q0_7, mem_unit_imthebeemoplush_1_q0_7, undriven;
  wire [10:0] bit_extender_2_out, inst_decoder_1_to_pc, PC_IN, PC_OUT;
  wire [31:0] inst_decoder_1_control_word;

  LED led_1 (.in(PC_IN[10]));
  LED led_2 (.in(PC_IN[9]));
  LED led_3 (.in(PC_IN[8]));
  LED led_4 (.in(PC_OUT[10]));
  LED led_5 (.in(PC_OUT[9]));
  LED led_6 (.in(PC_OUT[8]));
  LED led_7 (.in(PC_IN[7]));
  LED led_8 (.in(PC_IN[6]));
  LED led_9 (.in(PC_IN[5]));
  LED led_10 (.in(PC_IN[4]));
  LED led_11 (.in(PC_OUT[7]));
  LED led_12 (.in(PC_OUT[6]));
  LED led_13 (.in(PC_OUT[5]));
  LED led_14 (.in(PC_OUT[4]));
  DipSwitch #(.number(2)) dipswitch_1 (.sw1(dipswitch_1_sw2[1]), .sw2(dipswitch_1_sw2[0]));
  LED led_15 (.in(PC_IN[3]));
  LED led_16 (.in(PC_IN[2]));
  LED led_17 (.in(PC_IN[1]));
  LED led_18 (.in(PC_IN[0]));
  LED led_19 (.in(PC_OUT[3]));
  LED led_20 (.in(PC_OUT[2]));
  LED led_21 (.in(PC_OUT[1]));
  LED led_22 (.in(PC_OUT[0]));
  THE_CLOCK the_clock_1 (.SINGLE_STEP_IN(button_2_out), .SINGLE_STEP(in_5), .HLT(in_1), .CLK(CLK));  // open: nCLK
  Button button_1 (.out(MR));
  Button button_2 (.out(button_2_out));
  PROGRAM_COUNTER program_counter_1 (.CLK(CLK), .AD(PC_IN), .MR(MR), .JMP(in_2), .CE(in_3), .Q0_10(PC_OUT));
  assign PC_IN = inst_decoder_1_to_pc | bit_extender_2_out;  // OR_Gate or_1, 11 bits wide
  INST_DECODER inst_decoder_1 (
    .PROGRAM_SEL(dipswitch_1_sw2), .WE(INSTwe), .CLK(CLK), .PC(PC_OUT), .MR(MR), .OPERAND_DATA(in_7),
    .OPERAND_REG({in_6, in_4}), .FLAGS(FLAGS), .INST_DONE(in_21), .CONTROL_WORD(inst_decoder_1_control_word),
    .OPCODE(OPCODE), .TO_PC(inst_decoder_1_to_pc), .Q0_7(inst_decoder_1_q0_7), .INST_STEP(STEP));
  LED led_23 (.in(STEP[3]));
  LED led_24 (.in(STEP[2]));
  LED led_25 (.in(STEP[1]));
  LED led_26 (.in(STEP[0]));
  LED led_27 (.in(OPCODE[4]));
  LED led_28 (.in(OPCODE[3]));
  assign bit_extender_1_out = {{5{1'b0}}, PC_OUT[10:8]};  // Bit_Extender bit_extender_1
  Decoder #(.select(3)) decoder_1 (
    .out1(MEMwe), .out2(REGwe), .out3(MADwe), .out4(INSTwe), .out6(INAwe), .out7(INBwe),
    .sel({in_27, in_26, in_25}), .en(1'b1));  // open: out0, out5
  LED led_29 (.in(OPCODE[2]));
  LED led_30 (.in(OPCODE[1]));
  LED led_31 (.in(OPCODE[0]));
  LED led_32 (.in(controlled_buffer_1_out[7]));
  assign controlled_buffer_1_out = in_29 ? bit_extender_1_out : 8'bz;  // Controlled_Buffer controlled_buffer_1
  assign controlled_buffer_1_out = in_28 ? PC_OUT[7:0] : 8'bz;  // Controlled_Buffer controlled_buffer_2
  Bit_Extender #(.out_width(3)) bit_extender_2 (.in(controlled_buffer_1_out), .out(bit_extender_2_out[10:8]));
  assign controlled_buffer_1_out = in_8 ? inst_decoder_1_q0_7 : 8'bz;  // Controlled_Buffer controlled_buffer_3
  LED led_33 (.in(ALU_A[7]));
  LED led_34 (.in(ALU_A[6]));
  LED led_35 (.in(ALU_A[5]));
  LED led_36 (.in(ALU_B[7]));
  LED led_37 (.in(ALU_B[6]));
  LED led_38 (.in(ALU_B[5]));
  LED led_39 (.in(ALU_OUTPUT[7]));
  LED led_40 (.in(ALU_OUTPUT[6]));
  LED led_41 (.in(ALU_OUTPUT[5]));
  LED led_42 (.in(controlled_buffer_1_out[6]));
  LED led_43 (.in(controlled_buffer_1_out[5]));
  LED led_44 (.in(controlled_buffer_1_out[4]));
  LED led_45 (.in(controlled_buffer_1_out[3]));
  Register register_1 (.D(controlled_buffer_1_out), .en(in_30), .Q(bit_extender_2_out[7:0]), .clk(CLK), .clr(MR));
  Pull_Resistor pull_resistor_1 (.node(controlled_buffer_1_out));
  LED led_46 (.in(ALU_A[4]));
  LED led_47 (.in(ALU_A[3]));
  LED led_48 (.in(ALU_A[2]));
  LED led_49 (.in(ALU_A[1]));
  LED led_50 (.in(ALU_B[4]));
  LED led_51 (.in(ALU_B[3]));
  LED led_52 (.in(ALU_B[2]));
  LED led_53 (.in(ALU_B[1]));
  LED led_54 (.in(ALU_OUTPUT[4]));
  LED led_55 (.in(ALU_OUTPUT[3]));
  LED led_56 (.in(ALU_OUTPUT[2]));
  LED led_57 (.in(ALU_OUTPUT[1]));
  LED led_58 (.in(controlled_buffer_1_out[2]));
  LED led_59 (.in(controlled_buffer_1_out[1]));
  LED led_60 (.in(controlled_buffer_1_out[0]));
  LED led_61 (.in(ALU_A[0]));
  LED led_62 (.in(ALU_B[0]));
  LED led_63 (.in(ALU_OUTPUT[0]));
  assign controlled_buffer_1_out = in_16 ? undriven : 8'bz;  // Controlled_Buffer controlled_buffer_4
  assign controlled_buffer_5_out = in_24 ? undriven : 8'bz;  // Controlled_Buffer controlled_buffer_5
  assign controlled_buffer_6_out = in_23 ? controlled_buffer_1_out : 8'bz;  // Controlled_Buffer controlled_buffer_6
  assign controlled_buffer_1_out = in_22 ? mem_unit_imthebeemoplush_1_q0_7 : 8'bz;  // Controlled_Buffer controlled_buffer_7
  // ALU alu_1: pin names not known; wires that end beside it: controlled_buffer_5_out, in_10, controlled_buffer_5_out, in_10, in_11, in_12, in_13, in_14, CLK, ALU_A, ALU_B, in_15, in_15
  Mem_Unit_ImTheBeemoPlush mem_unit_imthebeemoplush_1 (
    .MWE(MEMwe), .D_U(in_19), .CE(in_20), .CLK(CLK), .MR(MR), .FUNC_SEL({in_18, in_17}),
    .AD(controlled_buffer_6_out), .ADWE(MADwe), .RWE(REGwe), .D(controlled_buffer_6_out),
    .Q0_7(mem_unit_imthebeemoplush_1_q0_7));  // open: STACK_POS, AD_OUT, DATA_OUT
  // Pins of 3 and 4 bits meet at FLAGS

  // Other names for the same wires on the sheet: HLT = in_1; JMP = in_2; PCe = in_3; REG_OUT[1:0] = {in_6, in_4};
  //   DATA_OUT = in_7; OPERAND_OUT = in_8; FLe = in_9; SUBe = in_10; ADDe = in_11; ANDe = in_12; XORe = in_13;
  //   NOTe = in_14; RSHe = in_15; ALU_OUT = in_16; FSEL[1:0] = {in_18, in_17}; ST_U_D = in_19; MCE = in_20;
  //   INST_DONE = in_21; MEM_OUT = in_22; MEM_IN = in_23; ALU_IN = in_24; PC_OUT0 = in_28; PC_OUT1 = in_29;
  //   PC_INwe = in_30; REGAD[2:0] = {in_27, in_26, in_25}

  // Notes on the sheet:
  //   PC
  //   CLOCK
  //   INSTRUCTION DECODER
  //   BUS
  //   ALU
  //   HEAP, STACK, REG
endmodule

module ALU (
  input  A_REGe,
  input  B_REGe,
  input  CLK,
  input  MR,
  input  NOTe,
  input  C_in,
  input  ADDe,
  input  ANDe,
  input  XORe,
  input  RSHe,
  input  ALUoe,
  input  FLAGe,
  input  [7:0] BUSin_ALU,
  output [7:0] REG_Bo,
  output [7:0] REG_Ao,
  output VF,
  output NF,
  output CF,
  output ZF,
  output [7:0] BUSout_ALU
);

  wire and_2_out, and_3_out;
  wire [3:0] or_1_out;
  wire [6:0] adder_1_out;
  wire [7:0] and_1_out, controlled_buffer_1_out, controlled_buffer_2_out, controlled_buffer_3_out,
       multiplexer_1_out, multiplexer_2_out, not_1_out, or_2_out, xor_1_out;
  wire [7:7] undriven;

  Register REG_A (.D(BUSin_ALU), .en(A_REGe), .clk(CLK), .Q(REG_Ao), .clr(MR));
  Register REG_B (.D(BUSin_ALU), .en(B_REGe), .clk(CLK), .Q(REG_Bo), .clr(MR));
  assign xor_1_out = REG_Ao ^ REG_Bo;  // XOR_Gate xor_1, 8 bits wide
  assign and_1_out = REG_Ao & REG_Bo;  // AND_Gate and_1, 8 bits wide
  Multiplexer #(.width(8)) multiplexer_1 (.in0(REG_Bo), .in1(not_1_out), .out(multiplexer_1_out), .sel(NOTe));
  assign not_1_out = ~REG_Bo;  // NOT_Gate not_1, 8 bits wide
  Adder adder_1 (.a(REG_Ao), .b(multiplexer_1_out), .out({or_1_out[1], adder_1_out}), .cin(C_in), .cout(or_1_out[2]));
  assign controlled_buffer_1_out = XORe ? xor_1_out : 8'bz;  // Controlled_Buffer controlled_buffer_1
  assign controlled_buffer_2_out = ANDe ? and_1_out : 8'bz;  // Controlled_Buffer controlled_buffer_2
  assign controlled_buffer_3_out = ADDe ? {or_1_out[1], adder_1_out} : 8'bz;  // Controlled_Buffer controlled_buffer_3
  Pull_Resistor pull_resistor_1 (.node(controlled_buffer_3_out));
  and and_2 (and_2_out, ~REG_Ao[7], ~multiplexer_1_out[7], or_1_out[1]);  // AND_Gate
  and and_3 (and_3_out, REG_Ao[7], multiplexer_1_out[7], ~or_1_out[1]);  // AND_Gate
  Pull_Resistor pull_resistor_2 (.node(controlled_buffer_2_out));
  Pull_Resistor pull_resistor_3 (.node(controlled_buffer_1_out));
  or or_1 (or_1_out[0], and_2_out, and_3_out);
  assign or_2_out = controlled_buffer_1_out | controlled_buffer_2_out | controlled_buffer_3_out;  // OR_Gate or_2, 8 bits wide
  Multiplexer #(.width(8)) multiplexer_2 (
    .in0(or_2_out), .in1({undriven[7], or_2_out[7:1]}), .out(multiplexer_2_out), .sel(RSHe));
  nor nor_1 (or_1_out[3], multiplexer_2_out[0], multiplexer_2_out[1], multiplexer_2_out[2], multiplexer_2_out[3], multiplexer_2_out[4], multiplexer_2_out[5], multiplexer_2_out[6], multiplexer_2_out[7]);
  assign BUSout_ALU = ALUoe ? multiplexer_2_out : 8'bz;  // Controlled_Buffer controlled_buffer_4
  Pull_Resistor pull_resistor_4 (.node(BUSout_ALU));
  Register #(.width(4)) register_1 (.D(or_1_out), .en(FLAGe), .clk(CLK), .Q({ZF, CF, NF, VF}), .clr(MR));

  // Notes on the sheet:
  //   MOHAMMED
endmodule

module PROGRAM_COUNTER (
  input  [10:0] AD,
  input  MR,
  input  JMP,
  input  CE,
  input  CLK,
  output [10:0] Q0_10
);

  Counter #(.max('h7ff), .width(11)) counter_1 (
    .clr(MR), .load(JMP), .up(1'b1), .count(CE), .clk(CLK), .D(AD), .Q(Q0_10));  // open: carry
endmodule

module INST_DECODER (
  input  [1:0] PROGRAM_SEL,
  input  [10:0] PC,
  input  WE,
  input  CLK,
  input  MR,
  input  [1:0] OPERAND_REG,
  input  OPERAND_DATA,
  input  [3:0] FLAGS,
  input  INST_DONE,
  output [10:0] TO_PC,
  output [4:0] OPCODE,
  output [7:0] Q0_7,
  output [31:0] CONTROL_WORD,
  output [3:0] INST_STEP
);

  wire not_1_out, or_1_out;
  wire [7:0] bit_extender_1_out, bit_extender_2_out, bit_extender_3_out, controlled_buffer_1_out, LOWER_data,
       multiplexer_1_out;
  wire [15:8] UPPER_data;

  not not_1 (not_1_out, CLK);
  Counter #(.max('hf), .width(4)) counter_1 (
    .count(1'b1), .Q(INST_STEP), .up(1'b1), .clk(not_1_out), .clr(or_1_out));  // open: load, D, carry
  or or_1 (or_1_out, MR, INST_DONE);
  ROM #(.addrWidth(13)) rom_1 (.addr({INST_STEP, FLAGS, OPCODE}), .data(CONTROL_WORD[7:0]));
  ROM #(.addrWidth(13)) rom_2 (.addr({INST_STEP, FLAGS, OPCODE}), .data(CONTROL_WORD[15:8]));
  ROM #(.addrWidth(13)) rom_3 (.addr({INST_STEP, FLAGS, OPCODE}), .data(CONTROL_WORD[23:16]));
  ROM #(.addrWidth(13)) rom_4 (.addr({INST_STEP, FLAGS, OPCODE}), .data(CONTROL_WORD[31:24]));
  ROM #(.addrWidth(13)) LOWER (.addr({PROGRAM_SEL, PC}), .data(LOWER_data));
  ROM #(.addrWidth(13)) UPPER (.addr({PROGRAM_SEL, PC}), .data(UPPER_data));
  Register #(.width(16)) register_1 (
    .D({UPPER_data, LOWER_data}), .en(WE), .clk(CLK),
    .Q({TO_PC[0], TO_PC[1], TO_PC[2], TO_PC[3], TO_PC[4], TO_PC[5], TO_PC[6], TO_PC[7], TO_PC[8], TO_PC[9], TO_PC[10], OPCODE[0], OPCODE[1], OPCODE[2], OPCODE[3], OPCODE[4]}),
    .clr(MR));
  assign controlled_buffer_1_out = OPERAND_DATA ? TO_PC[7:0] : 8'bz;  // Controlled_Buffer controlled_buffer_1
  assign bit_extender_1_out = {{5{1'b0}}, TO_PC[7:5]};  // Bit_Extender bit_extender_1
  assign bit_extender_2_out = {{5{1'b0}}, TO_PC[4:2]};  // Bit_Extender bit_extender_2
  assign bit_extender_3_out = {{5{1'b0}}, TO_PC[10:8]};  // Bit_Extender bit_extender_3
  Pull_Resistor pull_resistor_1 (.node(controlled_buffer_1_out));
  assign Q0_7 = controlled_buffer_1_out | multiplexer_1_out;  // OR_Gate or_2, 8 bits wide
  Multiplexer #(.select(2), .width(8)) multiplexer_1 (
    .in0({8{1'b0}}), .in1(bit_extender_3_out), .in2(bit_extender_1_out), .in3(bit_extender_2_out),
    .out(multiplexer_1_out), .sel(OPERAND_REG));

  // Notes on the sheet:
  //   contents of LOWER (hex, n*v repeats v):
  //   d 1e 0 11 1e 1f
  //   contents of UPPER (hex, n*v repeats v):
  //   50 40 ff a0 40
endmodule

module Mem_Unit_ImTheBeemoPlush (
  input  [1:0] FUNC_SEL,
  input  MWE,
  input  D_U,
  input  CE,
  input  CLK,
  input  MR,
  input  [7:0] D,
  input  RWE,
  input  [7:0] AD,
  input  ADWE,
  output [7:0] Q0_7,
  output [7:0] STACK_POS,
  output [7:0] AD_OUT,
  output [7:0] DATA_OUT
);

  wire not_1_out;
  wire [7:0] multiplexer_1_out, or_1_out;

  Counter counter_1 (.count(CE), .Q(STACK_POS), .up(D_U), .clk(CLK), .clr(MR));  // open: load, D, carry
  Multiplexer #(.width(8)) multiplexer_1 (.in0(AD_OUT), .in1(STACK_POS), .out(multiplexer_1_out), .sel(FUNC_SEL[1]));
  Register register_1 (.D(AD), .en(ADWE), .clk(CLK), .Q(AD_OUT), .clr(MR));
  not not_1 (not_1_out, MWE);
  RAM #(.addrWidth(13), .asyncread("true"), .clearpin("true"), .databus("bidir")) ram_1 (
    .addr({3'b000, FUNC_SEL, multiplexer_1_out}), .we(MWE), .oe(not_1_out), .clk(CLK), .data(Q0_7), .clr(MR));
  Register register_2 (.D(or_1_out), .en(RWE), .clk(CLK), .Q(DATA_OUT), .clr(MR));
  assign Q0_7 = MWE ? DATA_OUT : 8'bz;  // Controlled_Buffer controlled_buffer_1
  assign or_1_out = Q0_7 | D;  // OR_Gate or_1, 8 bits wide

  // Notes on the sheet:
  //   00  -   MEM
  //   01  -   REG
  //   10  - STACK
endmodule

module THE_CLOCK (
  input  SINGLE_STEP_IN,
  input  SINGLE_STEP,
  input  HLT,
  output CLK,
  output nCLK
);

  wire clock_1_out, multiplexer_1_out;

  Clock clock_1 (.out(clock_1_out));
  Multiplexer multiplexer_1 (.in0(SINGLE_STEP_IN), .in1(clock_1_out), .out(multiplexer_1_out), .sel(SINGLE_STEP));
  and and_1 (CLK, multiplexer_1_out, ~HLT);  // AND_Gate
  not not_1 (nCLK, CLK);
endmodule

module I_O_PORT (
  input  [7:0] X,
  input  [7:0] Y,
  input  [7:0] C,
  input  MR,
  input  CLK,
  input  SWE,
  input  [7:0] ADDRESS,
  input  [7:0] DATA,
  input  [7:0] Q0_7
);

  wire controlled_buffer_1_out, keyboard_1_avail, rgb_video_1_p4, rgb_video_1_p5;
  wire [3:0] undriven;
  wire [6:0] keyboard_1_data;

  Decoder #(.select(4)) decoder_1 (.sel(undriven));  // open: out0, out1, out2, out3, out4, out5, out6, out7, out8, out9, out10, out11, out12, out13, out14, out15, en
  Register register_1 (.D(ADDRESS));  // open: en, clk, Q, clr
  // RGB_Video #(.cursor("No Cursor"), .height(64), .scale(8), .width(64)) rgb_video_1: pin names not known; wires that end beside it: MR, CLK, SWE, rgb_video_1_p4, rgb_video_1_p5, C
  assign controlled_buffer_1_out = keyboard_1_avail ? CLK : 1'bz;  // Controlled_Buffer controlled_buffer_1
  Keyboard #(.buflen(128)) keyboard_1 (
    .clk(controlled_buffer_1_out), .re(1'b1), .clr(MR), .avail(keyboard_1_avail), .data(keyboard_1_data));
  TTY #(.cols(96), .rows(24)) tty_1 (.data(keyboard_1_data), .clk(CLK), .we(keyboard_1_avail), .clr(MR));
endmodule

module Mem_Unit_Gisen (
  input  [7:0] BUSin,
  input  MEM_SEL,
  input  UNIT_REGwe,
  input  CNTe,
  input  Dec0_Inc1,
  input  REG_STACK_SEL,
  input  MR,
  input  CLK,
  input  BANK_ADwe,
  input  MEMwe,
  input  MEM_ADwe,
  input  MEMoe,
  output [7:0] BANK_ADo,
  output [7:0] MEM_ADo,
  output [8:0] STACKpos,
  output [7:0] BUSout
);

  wire or_2_out;
  wire [1:0] demultiplexer_1_out0, demultiplexer_1_out1;
  wire [7:0] MEM_UNIT_REG_q, or_1_out, STACK_REG_data;
  wire [8:0] bit_extender_1_out, multiplexer_1_out;

  Counter #(.max('h1ff), .width(9)) counter_1 (
    .count(CNTe), .Q(STACKpos), .up(Dec0_Inc1), .clk(MR), .clr(CLK));  // open: load, D, carry
  Multiplexer #(.width(9)) multiplexer_1 (
    .in0(STACKpos), .in1(bit_extender_1_out), .out(multiplexer_1_out), .sel(REG_STACK_SEL));
  assign bit_extender_1_out = {{1{MEM_ADo[7]}}, MEM_ADo};  // Bit_Extender bit_extender_1
  RAM #(.addrWidth(10), .databus("bidir")) STACK_REG (
    .addr({REG_STACK_SEL, multiplexer_1_out}), .we(demultiplexer_1_out0[0]), .oe(demultiplexer_1_out0[1]),
    .clk(MR), .data(STACK_REG_data));
  Register BANK_AD_REG (.D(STACK_REG_data), .en(BANK_ADwe), .clk(MR), .Q(BANK_ADo), .clr(CLK));
  Register MEM_AD_REG (.D(STACK_REG_data), .en(MEM_ADwe), .clk(MR), .Q(MEM_ADo), .clr(CLK));
  RAM #(.addrWidth(11), .databus("bidir")) MEM (
    .addr({BANK_ADo[2:0], MEM_ADo}), .we(demultiplexer_1_out1[0]), .oe(demultiplexer_1_out1[1]), .clk(MR),
    .data(STACK_REG_data));
  Demultiplexer #(.width(2)) demultiplexer_1 (
    .out0(demultiplexer_1_out0), .out1(demultiplexer_1_out1), .in({MEMoe, MEMwe}), .sel(MEM_SEL));
  Pull_Resistor pull_resistor_1 (.node(STACK_REG_data));
  assign or_1_out = STACK_REG_data | BUSin;  // OR_Gate or_1, 8 bits wide
  or or_2 (or_2_out, MEM_ADwe, MEMwe, BANK_ADwe);
  Register MEM_UNIT_REG (.D(or_1_out), .en(UNIT_REGwe), .clk(MR), .Q(MEM_UNIT_REG_q), .clr(CLK));
  assign STACK_REG_data = or_2_out ? MEM_UNIT_REG_q : 8'bz;  // Controlled_Buffer controlled_buffer_1
  assign BUSout = MEMoe ? MEM_UNIT_REG_q : 8'bz;  // Controlled_Buffer controlled_buffer_2
endmodule

module Computer_Gisen (
  input  in_1,
  input  in_2,
  input  in_3,
  input  in_4,
  input  in_5,
  input  in_6,
  input  in_7,
  input  in_8,
  input  in_9,
  input  in_10,
  input  in_11,
  input  in_12,
  input  in_13,
  input  in_14,
  input  in_15,
  input  in_16,
  input  in_17,
  input  in_18,
  input  in_19,
  input  in_20,
  input  in_21,
  input  in_22,
  input  in_23,
  input  in_24,
  input  in_25,
  input  in_26,
  input  in_27,
  input  in_28,
  input  in_29,
  input  in_30,
  input  in_31,
  input  in_32,
  input  in_33
);

  wire button_2_out, CLK, INAwe, INBwe, INSTwe, MADwe, MEMwe, MR, REGwe;
  wire [1:0] dipswitch_1_sw2;
  wire [3:0] FLAGS, STEP;
  wire [4:0] OPCODE;
  wire [7:0] ALU_A, ALU_B, ALU_OUTPUT, bit_extender_1_out, controlled_buffer_1_out, controlled_buffer_4_out,
       inst_decoder_1_q0_7, undriven;
  wire [10:0] bit_extender_2_out, inst_decoder_1_to_pc, PC_IN, PC_OUT;
  wire [31:0] inst_decoder_1_control_word;

  LED led_1 (.in(PC_IN[10]));
  LED led_2 (.in(PC_IN[9]));
  LED led_3 (.in(PC_IN[8]));
  LED led_4 (.in(PC_OUT[10]));
  LED led_5 (.in(PC_OUT[9]));
  LED led_6 (.in(PC_OUT[8]));
  LED led_7 (.in(PC_IN[7]));
  LED led_8 (.in(PC_IN[6]));
  LED led_9 (.in(PC_IN[5]));
  LED led_10 (.in(PC_IN[4]));
  LED led_11 (.in(PC_OUT[7]));
  LED led_12 (.in(PC_OUT[6]));
  LED led_13 (.in(PC_OUT[5]));
  LED led_14 (.in(PC_OUT[4]));
  DipSwitch #(.number(2)) dipswitch_1 (.sw1(dipswitch_1_sw2[1]), .sw2(dipswitch_1_sw2[0]));
  LED led_15 (.in(PC_IN[3]));
  LED led_16 (.in(PC_IN[2]));
  LED led_17 (.in(PC_IN[1]));
  LED led_18 (.in(PC_IN[0]));
  LED led_19 (.in(PC_OUT[3]));
  LED led_20 (.in(PC_OUT[2]));
  LED led_21 (.in(PC_OUT[1]));
  LED led_22 (.in(PC_OUT[0]));
  THE_CLOCK the_clock_1 (.SINGLE_STEP_IN(button_2_out), .SINGLE_STEP(in_5), .HLT(in_1), .CLK(CLK));  // open: nCLK
  Button button_1 (.out(MR));
  Button button_2 (.out(button_2_out));
  PROGRAM_COUNTER program_counter_1 (.CLK(CLK), .AD(PC_IN), .MR(MR), .JMP(in_2), .CE(in_3), .Q0_10(PC_OUT));
  assign PC_IN = inst_decoder_1_to_pc | bit_extender_2_out;  // OR_Gate or_1, 11 bits wide
  INST_DECODER inst_decoder_1 (
    .PROGRAM_SEL(dipswitch_1_sw2), .WE(INSTwe), .CLK(CLK), .PC(PC_OUT), .MR(MR), .OPERAND_DATA(in_7),
    .OPERAND_REG({in_6, in_4}), .FLAGS(FLAGS), .INST_DONE(in_21), .CONTROL_WORD(inst_decoder_1_control_word),
    .OPCODE(OPCODE), .TO_PC(inst_decoder_1_to_pc), .Q0_7(inst_decoder_1_q0_7), .INST_STEP(STEP));
  LED led_23 (.in(STEP[3]));
  LED led_24 (.in(STEP[2]));
  LED led_25 (.in(STEP[1]));
  LED led_26 (.in(STEP[0]));
  LED led_27 (.in(OPCODE[4]));
  LED led_28 (.in(OPCODE[3]));
  assign bit_extender_1_out = {{5{1'b0}}, PC_OUT[10:8]};  // Bit_Extender bit_extender_1
  Decoder #(.select(3)) decoder_1 (
    .out1(MEMwe), .out2(REGwe), .out3(MADwe), .out4(INSTwe), .out6(INAwe), .out7(INBwe),
    .sel({in_27, in_26, in_25}), .en(1'b1));  // open: out0, out5
  LED led_29 (.in(OPCODE[2]));
  LED led_30 (.in(OPCODE[1]));
  LED led_31 (.in(OPCODE[0]));
  LED led_32 (.in(controlled_buffer_1_out[7]));
  assign controlled_buffer_1_out = in_29 ? bit_extender_1_out : 8'bz;  // Controlled_Buffer controlled_buffer_1
  assign controlled_buffer_1_out = in_28 ? PC_OUT[7:0] : 8'bz;  // Controlled_Buffer controlled_buffer_2
  Bit_Extender #(.out_width(3)) bit_extender_2 (.in(controlled_buffer_1_out), .out(bit_extender_2_out[10:8]));
  assign controlled_buffer_1_out = in_8 ? inst_decoder_1_q0_7 : 8'bz;  // Controlled_Buffer controlled_buffer_3
  LED led_33 (.in(ALU_A[7]));
  LED led_34 (.in(ALU_A[6]));
  LED led_35 (.in(ALU_A[5]));
  LED led_36 (.in(ALU_B[7]));
  LED led_37 (.in(ALU_B[6]));
  LED led_38 (.in(ALU_B[5]));
  LED led_39 (.in(ALU_OUTPUT[7]));
  LED led_40 (.in(ALU_OUTPUT[6]));
  LED led_41 (.in(ALU_OUTPUT[5]));
  LED led_42 (.in(controlled_buffer_1_out[6]));
  LED led_43 (.in(controlled_buffer_1_out[5]));
  LED led_44 (.in(controlled_buffer_1_out[4]));
  LED led_45 (.in(controlled_buffer_1_out[3]));
  Register register_1 (.D(controlled_buffer_1_out), .en(in_30), .Q(bit_extender_2_out[7:0]), .clk(CLK), .clr(MR));
  Pull_Resistor pull_resistor_1 (.node(controlled_buffer_1_out));
  LED led_46 (.in(ALU_A[4]));
  LED led_47 (.in(ALU_A[3]));
  LED led_48 (.in(ALU_A[2]));
  LED led_49 (.in(ALU_A[1]));
  LED led_50 (.in(ALU_B[4]));
  LED led_51 (.in(ALU_B[3]));
  LED led_52 (.in(ALU_B[2]));
  LED led_53 (.in(ALU_B[1]));
  LED led_54 (.in(ALU_OUTPUT[4]));
  LED led_55 (.in(ALU_OUTPUT[3]));
  LED led_56 (.in(ALU_OUTPUT[2]));
  LED led_57 (.in(ALU_OUTPUT[1]));
  LED led_58 (.in(controlled_buffer_1_out[2]));
  LED led_59 (.in(controlled_buffer_1_out[1]));
  LED led_60 (.in(controlled_buffer_1_out[0]));
  LED led_61 (.in(ALU_A[0]));
  LED led_62 (.in(ALU_B[0]));
  LED led_63 (.in(ALU_OUTPUT[0]));
  ALU alu_1 (
    .RSHe(in_15), .ALUoe(in_16), .FLAGe(in_9), .A_REGe(INAwe), .B_REGe(INBwe),
    .BUSin_ALU(controlled_buffer_1_out), .CLK(CLK), .MR(MR), .NOTe(in_14), .C_in(in_10), .ADDe(in_11),
    .ANDe(in_12), .XORe(in_13), .BUSout_ALU(controlled_buffer_1_out), .VF(FLAGS[3]), .NF(FLAGS[2]),
    .CF(FLAGS[1]), .ZF(FLAGS[0]));  // open: REG_Bo, REG_Ao
  assign controlled_buffer_4_out = in_23 ? controlled_buffer_1_out : 8'bz;  // Controlled_Buffer controlled_buffer_4
  assign controlled_buffer_1_out = in_22 ? undriven : 8'bz;  // Controlled_Buffer controlled_buffer_5
  Mem_Unit_Gisen mem_unit_gisen_1 ();  // open: BUSin, MEM_SEL, UNIT_REGwe, CNTe, Dec0_Inc1, REG_STACK_SEL, MR, CLK, BANK_ADwe, MEMwe, MEM_ADwe, MEMoe, BANK_ADo, MEM_ADo, STACKpos, BUSout

  // Other names for the same wires on the sheet: HLT = in_1; JMP = in_2; PCe = in_3; REG_OUT[1:0] = {in_6, in_4};
  //   DATA_OUT = in_7; OPERAND_OUT = in_8; FLe = in_9; C_IN = in_10; ADDe = in_11; ANDe = in_12; XORe = in_13;
  //   NOTe = in_14; RSHe = in_15; ALU_OUT = in_16; FSEL[1:0] = {in_18, in_17}; ST_U_D = in_19; MCE = in_20;
  //   INST_DONE = in_21; MEM_OUT = in_22; MEM_IN = in_23; ALU_IN = in_24; PC_OUT0 = in_28; PC_OUT1 = in_29;
  //   PC_INwe = in_30; REGAD[2:0] = {in_27, in_26, in_25}

  // Notes on the sheet:
  //   PC
  //   CLOCK
  //   INSTRUCTION DECODER
  //   BUS
  //   HEAP, STACK, REG
  //   ALU
endmodule
